# Fritzing sketch ir-remote (saved by Fritzing 0.7.5b)
breadboards: 1

parts:
  Arduino1 = Arduino
  R1 = Resistor [tolerance=±5% resistance=100 package=THT]
  LED1 = LED - 3mm [color="Infrared (880nm)" package="3 mm [THT]"]

nets:
  N1: Arduino1.D9, R1.Pin_0
  N2: Arduino1.GND, LED1.anode
  N3: R1.Pin_1, LED1.cathode
